// Logisim project ALU1.circ as structural Verilog: 1 circuit, main circuit main
// Alu
module main (
  input  [15:0] Bus_A,
  input  [15:0] Bus_B,
  input  [1:0] Function_bit,
  input  [1:0] Alu_Selection,
  input  [2:0] Branch_Selection,
  output Branch,
  output [15:0] Bus_w
);

  wire adder_1_cout, comparator_1_eq, comparator_1_gt, comparator_2_lt;
  wire [15:0] adder_1_out, adder_2_out, and_1_out, bit_extender_1_out, bit_extender_2_out,
       bit_extender_3_out, bit_extender_4_out, main_1_output, multiplexer_1_out, multiplexer_2_out,
       multiplexer_3_out, not_1_out, or_1_out, shifter_1_out, shifter_2_out, shifter_3_out, xor_1_out,
       xor_2_out;

  assign bit_extender_1_out = {{15{1'b1}}, 1'b1};  // Bit_Extender bit_extender_1
  assign xor_1_out = Bus_B ^ bit_extender_1_out;  // XOR_Gate xor_1, 16 bits wide
  Shifter #(.width(16)) shifter_1 (.in(Bus_A), .\dist (Bus_B[3:0]), .out(shifter_1_out));
  Shifter #(.width(16), .shift("lr")) shifter_2 (.in(Bus_A), .\dist (Bus_B[3:0]), .out(shifter_2_out));
  Shifter #(.width(16), .shift("ar")) shifter_3 (.in(Bus_A), .\dist (Bus_B[3:0]), .out(shifter_3_out));
  Adder #(.width(16)) adder_1 (.a(Bus_A), .b(Bus_B), .out(adder_1_out), .cout(adder_1_cout));  // open: cin
  assign and_1_out = Bus_B & Bus_A;  // AND_Gate and_1, 16 bits wide
  assign or_1_out = Bus_B | Bus_A;  // OR_Gate or_1, 16 bits wide
  assign not_1_out = ~or_1_out;  // NOT_Gate not_1, 16 bits wide
  assign xor_2_out = Bus_B ^ Bus_A;  // XOR_Gate xor_2, 16 bits wide
  Adder #(.width(16)) adder_2 (.a(Bus_A), .b(xor_1_out), .out(adder_2_out), .cin(1'b1));  // open: cout
  Comparator #(.width(16)) comparator_1 (.a(Bus_A), .b(Bus_B), .gt(comparator_1_gt), .eq(comparator_1_eq));  // open: lt
  Multiplexer #(.select(2), .width(16)) multiplexer_1 (
    .in0(and_1_out), .in1(or_1_out), .in2(xor_2_out), .in3(not_1_out), .out(multiplexer_1_out),
    .sel(Function_bit));  // open: en
  assign bit_extender_2_out = {{15{1'b0}}, comparator_1_gt};  // Bit_Extender bit_extender_2
  assign bit_extender_3_out = {{15{1'b0}}, comparator_1_eq};  // Bit_Extender bit_extender_3
  Branch_comparator_main main_1 (.bus_A(Bus_A), .Selelction(Branch_Selection), .Branch(Branch), .Output(main_1_output));
  Multiplexer #(.select(2), .width(16)) multiplexer_2 (
    .in0(shifter_1_out), .in1(shifter_2_out), .out(multiplexer_2_out), .sel(Function_bit));  // open: in2, in3, en
  Comparator #(.width(1)) comparator_2 (.a(adder_1_out[15]), .b(adder_1_cout), .lt(comparator_2_lt));  // open: gt, eq
  Multiplexer #(.select(2), .width(16)) multiplexer_3 (
    .in0(adder_1_out), .in1(adder_2_out), .in2(bit_extender_2_out), .in3(bit_extender_3_out),
    .out(multiplexer_3_out), .sel(Function_bit));  // open: en
  assign bit_extender_4_out = {{15{1'b0}}, comparator_2_lt};  // Bit_Extender bit_extender_4
  Multiplexer #(.select(2), .width(16)) multiplexer_4 (
    .in0(main_1_output), .in1(multiplexer_2_out), .in2(multiplexer_1_out), .in3(multiplexer_3_out),
    .out(Bus_w), .sel(Alu_Selection));  // open: en

  // Notes on the sheet:
  //   Logical Operation
  //   Alu Selexction
  //   Bus A
  //   Add/Sub
endmodule
