// Logisim project ALu controller.circ as structural Verilog: 1 circuit, main circuit main
module main (
  input  [4:0] Op_code,
  input  [1:0] Function_bit,
  output [2:0] Branch_output,
  output [1:0] Function_bit_2,
  output [1:0] Alu_Selection
);

  wire and_1_out, and_2_out, b_type_dectector_1_b, i_type_without_shifter_1_i, J_type_out, lw_out,
       R_type_out, sw_out;

  assign Function_bit_2 = R_type_out ? Function_bit : 2'bz;  // Controlled_Buffer controlled_buffer_1
  and R_type (R_type_out, ~Op_code[4], ~Op_code[3], ~Op_code[2], ~Op_code[1]);  // AND_Gate
  assign Alu_Selection = R_type_out ? {1'b1, Op_code[0]} : 2'bz;  // Controlled_Buffer controlled_buffer_2
  I_type_without_shifter i_type_without_shifter_1 (
    .A4(Op_code[4]), .A3(Op_code[3]), .A2(Op_code[2]), .A1(Op_code[1]), .A0(Op_code[0]),
    .I(i_type_without_shifter_1_i));
  and lw (lw_out, Op_code[4], ~Op_code[3], ~Op_code[2], ~Op_code[1], ~Op_code[0]);  // AND_Gate
  assign Function_bit_2 = lw_out ? Op_code[2:1] : 2'bz;  // Controlled_Buffer controlled_buffer_3
  assign Function_bit_2 = i_type_without_shifter_1_i ? Op_code[1:0] : 2'bz;  // Controlled_Buffer controlled_buffer_4
  assign Alu_Selection = i_type_without_shifter_1_i ? {1'b1, Op_code[3]} : 2'bz;  // Controlled_Buffer controlled_buffer_5
  and sw (sw_out, Op_code[4], ~Op_code[3], ~Op_code[2], ~Op_code[1], Op_code[0]);  // AND_Gate
  assign Function_bit_2 = sw_out ? Op_code[2:1] : 2'bz;  // Controlled_Buffer controlled_buffer_6
  assign Alu_Selection = lw_out ? 2'b11 : 2'bz;  // Controlled_Buffer controlled_buffer_7
  and J_type (J_type_out, Op_code[4], Op_code[3], Op_code[2], Op_code[1]);
  assign Alu_Selection = sw_out ? 2'b11 : 2'bz;  // Controlled_Buffer controlled_buffer_8
  assign Branch_output = b_type_dectector_1_b ? {Op_code[3], Op_code[1:0]} : 3'bz;  // Controlled_Buffer controlled_buffer_9
  assign Alu_Selection = b_type_dectector_1_b ? 2'b00 : 2'bz;  // Controlled_Buffer controlled_buffer_10
  B_type_Dectector b_type_dectector_1 (
    .A4(Op_code[4]), .A3(Op_code[3]), .A2(Op_code[2]), .A1(Op_code[1]), .A0(Op_code[0]),
    .B(b_type_dectector_1_b));
  and and_1 (and_1_out, ~Op_code[4], Op_code[3], Op_code[2], ~Op_code[1], ~Op_code[0]);  // AND_Gate
  assign Function_bit_2 = and_1_out ? Op_code[1:0] : 2'bz;  // Controlled_Buffer controlled_buffer_11
  assign Function_bit_2 = and_2_out ? {2{Op_code[1]}} : 2'bz;  // Controlled_Buffer controlled_buffer_12
  assign Alu_Selection = and_1_out ? 2'b01 : 2'bz;  // Controlled_Buffer controlled_buffer_13
  and and_2 (and_2_out, ~Op_code[4], Op_code[3], Op_code[2], ~Op_code[1], Op_code[0]);  // AND_Gate
  assign Alu_Selection = and_2_out ? 2'b01 : 2'bz;  // Controlled_Buffer controlled_buffer_14
endmodule
