// Logisim project ALu register.circ as structural Verilog: 1 circuit, main circuit main
module main (
  input  [15:0] PC_in,
  input  [15:0] PC_4_in,
  input  [15:0] IR_in,
  input  selPC_in,
  input  RF_Din_in,
  input  MemWrite_in,
  input  RegWrite_in,
  input  [15:0] Lo_in,
  input  [15:0] Hi_in,
  input  Branch_in,
  input  equal_in,
  input  [15:0] S_EXT_in,
  input  [2:0] halt_in,
  input  [15:0] ALU_out_in,
  input  [15:0] Addr_in,
  input  [15:0] RF_R1_in,
  input  [15:0] RF_R2_in,
  input  clk,
  input  clear,
  output [15:0] PC_out,
  output [15:0] PC_4_out,
  output [15:0] IR_out,
  output selPC_out,
  output RW__in,
  output RW__out,
  output RF_Din_out,
  output MemWrite_out,
  output RegWrite_out,
  output [15:0] Lo_out,
  output [15:0] Hi_out,
  output Branch_out,
  output equal_out,
  output [15:0] S_EXT_out,
  output [2:0] halt_out,
  output [15:0] ALU_out_out,
  output [15:0] Addr_out,
  output [15:0] RF_R1_out,
  output [15:0] RF_R2_out
);

  Register #(.width(16)) register_1 (.D(PC_in), .en(1'b1), .Q(PC_out), .clk(clk), .clr(clear));
  Register #(.width(16)) register_2 (.D(PC_4_in), .en(1'b1), .Q(PC_4_out), .clk(clk), .clr(clear));
  Register #(.width(16)) register_3 (.D(IR_in), .en(1'b1), .Q(IR_out), .clk(clk), .clr(clear));
  Register #(.width(1)) register_4 (.D(selPC_in), .en(1'b1), .Q(selPC_out), .clk(clk), .clr(clear));
  Register #(.width(1)) register_5 (.D(RW__in), .en(1'b1), .Q(RW__out), .clk(clk), .clr(clear));
  Register #(.width(1)) register_6 (.D(RF_Din_in), .en(1'b1), .Q(RF_Din_out), .clk(clk), .clr(clear));
  Register #(.width(1)) register_7 (.D(MemWrite_in), .en(1'b1), .Q(MemWrite_out), .clk(clk), .clr(clear));
  Register #(.width(1)) register_8 (.D(RegWrite_in), .en(1'b1), .Q(RegWrite_out), .clk(clk), .clr(clear));
  Register #(.width(16)) register_9 (.D(Lo_in), .en(1'b1), .Q(Lo_out), .clk(clk), .clr(clear));
  Register #(.width(16)) register_10 (.D(Hi_in), .en(1'b1), .Q(Hi_out), .clk(clk), .clr(clear));
  Register #(.width(1)) register_11 (.D(Branch_in), .en(1'b1), .Q(Branch_out), .clk(clk), .clr(clear));
  Register #(.width(1)) register_12 (.D(equal_in), .en(1'b1), .Q(equal_out), .clk(clk), .clr(clear));
  Register #(.width(16)) register_13 (.D(S_EXT_in), .en(1'b1), .Q(S_EXT_out), .clk(clk), .clr(clear));
  Register #(.width(3)) register_14 (.D(halt_in), .en(1'b1), .Q(halt_out), .clk(clk), .clr(clear));
  Register #(.width(16)) register_15 (.D(ALU_out_in), .en(1'b1), .Q(ALU_out_out), .clk(clk), .clr(clear));
  Register #(.width(16)) register_16 (.D(Addr_in), .en(1'b1), .Q(Addr_out), .clk(clk), .clr(clear));
  Register #(.width(16)) register_17 (.D(RF_R1_in), .en(1'b1), .Q(RF_R1_out), .clk(clk), .clr(clear));
  Register #(.width(16)) register_18 (.D(RF_R2_in), .en(1'b1), .Q(RF_R2_out), .clk(clk), .clr(clear));
endmodule
