// Logisim project Control unit.circ as structural Verilog: 1 circuit, main circuit main
module main (
  input  [4:0] in_1,
  output regDst,
  output RegWr,
  output Extop,
  output AluSrc,
  output MemRd,
  output MemWr,
  output WBdata,
  output J_Instruction
);

  wire b_type_dectector_1_b, I_type_i;

  and R_type (regDst, ~in_1[4], ~in_1[3], ~in_1[2], ~in_1[1]);  // AND_Gate
  I_type_Detectot I_type (.A4(in_1[4]), .A3(in_1[3]), .A2(in_1[2]), .A1(in_1[1]), .A0(in_1[0]), .I(I_type_i));
  and lw (MemRd, in_1[4], ~in_1[3], ~in_1[2], ~in_1[1], ~in_1[0]);  // AND_Gate
  and sw (MemWr, in_1[4], ~in_1[3], ~in_1[2], ~in_1[1], in_1[0]);  // AND_Gate
  and J_type (J_Instruction, in_1[4], in_1[3], in_1[2], in_1[1]);
  B_type_Dectector b_type_dectector_1 (
    .A4(in_1[4]), .A3(in_1[3]), .A2(in_1[2]), .A1(in_1[1]), .A0(in_1[0]), .B(b_type_dectector_1_b));
  or or_1 (RegWr, regDst, MemRd, I_type_i);
  or or_2 (Extop, I_type_i, b_type_dectector_1_b, MemWr, MemRd);
  or or_3 (AluSrc, I_type_i, MemWr, MemRd);

  assign WBdata = MemRd;
endmodule
