// Logisim project Data registers.circ as structural Verilog: 1 circuit, main circuit main
module main (
  input  in_1,
  input  in_2,
  input  [2:0] in_3,
  input  [15:0] in_4,
  input  [15:0] in_5,
  input  in_6,
  input  in_7,
  output [2:0] out_8,
  output [15:0] out_9,
  output [15:0] out_10,
  output out_11,
  output out_12
);

  Register #(.width(3)) register_1 (.D(in_3), .en(1'b1), .Q(out_8), .clk(in_1), .clr(in_2));
  Register #(.width(16)) register_2 (.D(in_4), .en(1'b1), .Q(out_9), .clk(in_1), .clr(in_2));
  Register #(.width(16)) register_3 (.D(in_5), .en(1'b1), .Q(out_10), .clk(in_1), .clr(in_2));
  Register #(.width(1)) register_4 (.D(in_6), .en(1'b1), .Q(out_11), .clk(in_1), .clr(in_2));
  Register #(.width(1)) register_5 (.D(in_7), .en(1'b1), .Q(out_12), .clk(in_1), .clr(in_2));
endmodule
