// Logisim project Memory_register.circ as structural Verilog: 1 circuit, main circuit main
module main (
  input  [15:0] PC_in,
  input  [15:0] PC_4_in,
  input  [15:0] IR_in,
  input  regDst,
  input  RegWr,
  input  Extop,
  input  AluSrc,
  input  MemRd,
  input  MemWrite_in,
  input  Wbdata,
  input  jump,
  input  [4:0] Op_code,
  input  [1:0] function_bit,
  input  [15:0] IMM_in,
  input  [15:0] Addr_in,
  input  [2:0] shamt_in,
  input  [15:0] v0_in,
  input  [15:0] a0_in,
  input  [15:0] RF_R1_in,
  input  [15:0] RF_R2_in,
  input  clk,
  input  clear,
  output [15:0] PC_out,
  output [15:0] PC_4_out,
  output [15:0] IR_out,
  output regDst_2,
  output RegWr_2,
  output Extop_2,
  output AluSrc_2,
  output MemRd_2,
  output MemWrite_out,
  output Wbdata_2,
  output jump_2,
  output [4:0] Op_code_2,
  output [1:0] function_bit_2,
  output [15:0] IMM_out,
  output [15:0] Addr_out,
  output [2:0] shamt_out,
  output [15:0] v0_out,
  output [15:0] a0_out,
  output [15:0] RF_R1_out,
  output [15:0] RF_R2_out
);

  Register #(.width(16)) register_1 (.D(PC_in), .en(1'b1), .Q(PC_out), .clk(clk), .clr(clear));
  Register #(.width(16)) register_2 (.D(PC_4_in), .en(1'b1), .Q(PC_4_out), .clk(clk), .clr(clear));
  Register #(.width(16)) register_3 (.D(IR_in), .en(1'b1), .Q(IR_out), .clk(clk), .clr(clear));
  Register #(.width(1)) register_4 (.D(regDst), .en(1'b1), .Q(regDst_2), .clk(clk), .clr(clear));
  Register #(.width(1)) register_5 (.D(RegWr), .en(1'b1), .Q(RegWr_2), .clk(clk), .clr(clear));
  Register #(.width(1)) register_6 (.D(Extop), .en(1'b1), .Q(Extop_2), .clk(clk), .clr(clear));
  Register #(.width(1)) register_7 (.D(AluSrc), .en(1'b1), .Q(AluSrc_2), .clk(clk), .clr(clear));
  Register #(.width(1)) register_8 (.D(MemRd), .en(1'b1), .Q(MemRd_2), .clk(clk), .clr(clear));
  Register #(.width(1)) register_9 (.D(MemWrite_in), .en(1'b1), .Q(MemWrite_out), .clk(clk), .clr(clear));
  Register #(.width(1)) register_10 (.D(Wbdata), .en(1'b1), .Q(Wbdata_2), .clk(clk), .clr(clear));
  Register #(.width(1)) register_11 (.D(jump), .en(1'b1), .Q(jump_2), .clk(clk), .clr(clear));
  Register #(.width(5)) register_12 (.D(Op_code), .en(1'b1), .Q(Op_code_2), .clk(clk), .clr(clear));
  Register #(.width(2)) register_13 (.D(function_bit), .en(1'b1), .Q(function_bit_2), .clk(clk), .clr(clear));
  Register #(.width(16)) register_14 (.D(IMM_in), .en(1'b1), .Q(IMM_out), .clk(clk), .clr(clear));
  Register #(.width(16)) register_15 (.D(Addr_in), .en(1'b1), .Q(Addr_out), .clk(clk), .clr(clear));
  Register #(.width(3)) register_16 (.D(shamt_in), .en(1'b1), .Q(shamt_out), .clk(clk), .clr(clear));
  Register #(.width(16)) register_17 (.D(v0_in), .en(1'b1), .Q(v0_out), .clk(clk), .clr(clear));
  Register #(.width(16)) register_18 (.D(a0_in), .en(1'b1), .Q(a0_out), .clk(clk), .clr(clear));
  Register #(.width(16)) register_19 (.D(RF_R1_in), .en(1'b1), .Q(RF_R1_out), .clk(clk), .clr(clear));
  Register #(.width(16)) register_20 (.D(RF_R2_in), .en(1'b1), .Q(RF_R2_out), .clk(clk), .clr(clear));
endmodule
