// Logisim project R-type instruction.circ as structural Verilog: 1 circuit, main circuit main
module main (
  input  in_1,
  input  in_2,
  input  in_3,
  input  in_4,
  input  [15:0] in_5,
  output [15:0] out_6,
  output [15:0] out_7,
  output [15:0] out_8
);

  wire [15:0] counter_1_q, ram_1_data;

  Counter #(.width(16), .max('hffff)) counter_1 (
    .Q(counter_1_q), .clk(in_1), .clr(in_2));  // open: load, D, count, carry
  RAM #(.addrWidth(16), .dataWidth(16)) ram_1 (
    .addr(counter_1_q), .data(ram_1_data), .clk(in_1));  // open: sel, ld, clr
  memory_element_main main_1 (
    .in_1(ram_1_data[10:8]), .in_2(ram_1_data[7:5]), .R_W(ram_1_data[4:2]), .in_4(in_5), .in_5(in_4),
    .clock(in_1), .out_7(out_7), .out_8(out_8));
  // ALU_main main_2: pin names not known; wires that end beside it: ram_1_data[1], ram_1_data[15:11], out_7, out_8, in_3, ram_1_data[1:0], out_6, in_3
endmodule
