// Logisim project if_id.circ as structural Verilog: 1 circuit, main circuit main
module main (
  input  [15:0] PC_in,
  input  [15:0] PC_4_in,
  input  [15:0] IR_in,
  input  clk,
  input  clear,
  output [15:0] PC_out,
  output [15:0] PC_4_out,
  output [15:0] IR_out
);

  Register #(.width(16)) register_1 (.D(PC_in), .en(1'b1), .Q(PC_out), .clk(clk), .clr(clear));
  Register #(.width(16)) register_2 (.D(PC_4_in), .en(1'b1), .Q(PC_4_out), .clk(clk), .clr(clear));
  Register #(.width(16)) register_3 (.D(IR_in), .en(1'b1), .Q(IR_out), .clk(clk), .clr(clear));
endmodule
