// Logisim project memory element.circ as structural Verilog: 1 circuit, main circuit main
module main (
  input  [2:0] in_1,
  input  [2:0] in_2,
  input  [2:0] R_W,
  input  [15:0] in_4,
  input  in_5,
  input  clock,
  output [15:0] out_7,
  output [15:0] out_8
);

  wire and_1_out, and_2_out, and_3_out, and_4_out, and_5_out, and_6_out, and_7_out, and_8_out,
       decoder_1_out0, decoder_1_out1, decoder_1_out2, decoder_1_out3, decoder_1_out4, decoder_1_out5,
       decoder_1_out6, decoder_1_out7, decoder_2_out0, decoder_2_out1, decoder_2_out2, decoder_2_out3,
       decoder_2_out4, decoder_2_out5, decoder_2_out6, decoder_2_out7, decoder_3_out0, decoder_3_out1,
       decoder_3_out2, decoder_3_out3, decoder_3_out4, decoder_3_out5, decoder_3_out6, decoder_3_out7;
  wire [15:0] register_1_q, register_2_q, register_3_q, register_4_q, register_5_q, register_6_q,
       register_7_q, register_8_q;

  Decoder #(.select(3)) decoder_1 (
    .out0(decoder_1_out0), .out1(decoder_1_out1), .out2(decoder_1_out2), .out3(decoder_1_out3),
    .out4(decoder_1_out4), .out5(decoder_1_out5), .out6(decoder_1_out6), .out7(decoder_1_out7), .sel(R_W));  // open: en
  and and_1 (and_1_out, decoder_1_out0, in_5);
  Register #(.width(16)) register_1 (.D(in_4), .en(and_1_out), .Q(register_1_q), .clk(clock));  // open: clr
  and and_2 (and_2_out, decoder_1_out1, in_5);
  Register #(.width(16)) register_2 (.D(in_4), .en(and_2_out), .Q(register_2_q), .clk(clock));  // open: clr
  and and_3 (and_3_out, decoder_1_out2, in_5);
  Register #(.width(16)) register_3 (.D(in_4), .en(and_3_out), .Q(register_3_q), .clk(clock));  // open: clr
  and and_4 (and_4_out, decoder_1_out3, in_5);
  and and_5 (and_5_out, decoder_1_out4, in_5);
  Register #(.width(16)) register_4 (.D(in_4), .en(and_4_out), .Q(register_4_q), .clk(clock));  // open: clr
  and and_6 (and_6_out, decoder_1_out5, in_5);
  Register #(.width(16)) register_5 (.D(in_4), .en(and_5_out), .Q(register_5_q), .clk(clock));  // open: clr
  and and_7 (and_7_out, decoder_1_out6, in_5);
  and and_8 (and_8_out, decoder_1_out7, in_5);
  Register #(.width(16)) register_6 (.D(in_4), .en(and_6_out), .Q(register_6_q), .clk(clock));  // open: clr
  Register #(.width(16)) register_7 (.D(in_4), .en(and_7_out), .Q(register_7_q), .clk(clock));  // open: clr
  assign out_7 = decoder_2_out0 ? register_1_q : 16'bz;  // Controlled_Buffer controlled_buffer_1
  Register #(.width(16)) register_8 (.D(in_4), .en(and_8_out), .Q(register_8_q), .clk(clock));  // open: clr
  assign out_7 = decoder_2_out1 ? register_2_q : 16'bz;  // Controlled_Buffer controlled_buffer_2
  assign out_7 = decoder_2_out2 ? register_3_q : 16'bz;  // Controlled_Buffer controlled_buffer_3
  assign out_7 = decoder_2_out3 ? register_4_q : 16'bz;  // Controlled_Buffer controlled_buffer_4
  assign out_7 = decoder_2_out4 ? register_5_q : 16'bz;  // Controlled_Buffer controlled_buffer_5
  Decoder #(.select(3)) decoder_2 (
    .out0(decoder_2_out0), .out1(decoder_2_out1), .out2(decoder_2_out2), .out3(decoder_2_out3),
    .out4(decoder_2_out4), .out5(decoder_2_out5), .out6(decoder_2_out6), .out7(decoder_2_out7), .sel(in_1));  // open: en
  assign out_7 = decoder_2_out5 ? register_6_q : 16'bz;  // Controlled_Buffer controlled_buffer_6
  assign out_7 = decoder_2_out6 ? register_7_q : 16'bz;  // Controlled_Buffer controlled_buffer_7
  assign out_7 = decoder_2_out7 ? register_8_q : 16'bz;  // Controlled_Buffer controlled_buffer_8
  assign out_8 = decoder_3_out0 ? register_1_q : 16'bz;  // Controlled_Buffer controlled_buffer_9
  assign out_8 = decoder_3_out1 ? register_2_q : 16'bz;  // Controlled_Buffer controlled_buffer_10
  assign out_8 = decoder_3_out2 ? register_3_q : 16'bz;  // Controlled_Buffer controlled_buffer_11
  assign out_8 = decoder_3_out3 ? register_4_q : 16'bz;  // Controlled_Buffer controlled_buffer_12
  assign out_8 = decoder_3_out4 ? register_5_q : 16'bz;  // Controlled_Buffer controlled_buffer_13
  Decoder #(.select(3)) decoder_3 (
    .out0(decoder_3_out0), .out1(decoder_3_out1), .out2(decoder_3_out2), .out3(decoder_3_out3),
    .out4(decoder_3_out4), .out5(decoder_3_out5), .out6(decoder_3_out6), .out7(decoder_3_out7), .sel(in_2));  // open: en
  assign out_8 = decoder_3_out5 ? register_6_q : 16'bz;  // Controlled_Buffer controlled_buffer_14
  assign out_8 = decoder_3_out6 ? register_7_q : 16'bz;  // Controlled_Buffer controlled_buffer_15
  assign out_8 = decoder_3_out7 ? register_8_q : 16'bz;  // Controlled_Buffer controlled_buffer_16
  Controlled_Buffer controlled_buffer_17 (.in(1'b0));  // open: out, en

  // Notes on the sheet:
  //   RA
  //   RB
  //   Reg write
  //   !6 bit input
endmodule
