// Logisim project pipeline.circ as structural Verilog: 1 circuit, main circuit main
module main (
  input  in_1,
  input  in_2,
  input  [15:0] in_3,
  input  in_4,
  output [15:0] out_5,
  output [15:0] out_6,
  output [15:0] out_7,
  output [15:0] out_8
);

  wire Branch, Jump, main_2_alusrc, main_2_extop, main_2_j_instruction, main_2_memrd, main_2_memwr,
       main_2_regdst, main_2_regwr, main_2_wbdata, main_4_alusrc_2, main_4_memrd_2, main_4_memwrite_out,
       main_4_regwr_2, main_4_wbdata_2, main_7_memwrite_out, main_7_regwrite_out, main_7_rf_din_out,
       main_7_selpc_out, main_8_selpc_out, not_1_out, not_2_out, or_1_out, or_2_out, or_3_out;
  wire [1:0] main_4_function_bit_2, main_6_alu_selection, main_6_function_bit_2;
  wire [2:0] main_4_shamt_out, main_6_branch_output, main_7_halt_out, main_8_reg_dest, multiplexer_1_out;
  wire [4:0] main_4_op_code_2;
  wire [15:0] bit_extender_1_out, bit_extender_2_out, bit_extender_3_out, counter_1_q, data, main_1_ir_out,
       main_1_pc_4_out, main_1_pc_out, main_4_a0_out, main_4_imm_out, main_4_ir_out, main_4_pc_4_out,
       main_4_pc_out, main_4_rf_r1_out, main_4_rf_r2_out, main_4_v0_out, main_7_ir_out, main_7_pc_4_out,
       main_7_pc_out, main_7_rf_r1_out, main_7_rf_r2_out, multiplexer_2_out, multiplexer_3_out,
       multiplexer_5_out, ram_1_data, rom_1_data;

  or or_1 (or_1_out, Branch, Jump);
  not not_1 (not_1_out, or_1_out);
  Counter #(.width(16), .max('hffff)) counter_1 (
    .load(or_1_out), .D(data), .count(not_1_out), .Q(counter_1_q), .clk(in_1), .clr(in_2));  // open: carry
  ROM #(.addrWidth(16), .dataWidth(16)) rom_1 (.addr(counter_1_q), .data(rom_1_data));  // open: sel
  if_id_main main_1 (
    .IR_in(rom_1_data), .clk(in_1), .PC_out(main_1_pc_out), .PC_4_out(main_1_pc_4_out), .IR_out(main_1_ir_out));  // open: PC_in, PC_4_in, clear
  Control_unit_main main_2 (
    .in_1(main_1_ir_out[15:11]), .J_Instruction(main_2_j_instruction), .regDst(main_2_regdst),
    .RegWr(main_2_regwr), .Extop(main_2_extop), .AluSrc(main_2_alusrc), .MemRd(main_2_memrd),
    .MemWr(main_2_memwr), .WBdata(main_2_wbdata));
  assign bit_extender_1_out = {{11{1'b0}}, main_1_ir_out[4:0]};  // Bit_Extender bit_extender_1
  Multiplexer #(.width(3)) multiplexer_1 (
    .in0(main_1_ir_out[7:5]), .in1(main_1_ir_out[4:2]), .out(multiplexer_1_out), .sel(main_2_regdst));  // open: en
  memory_element_main main_3 (
    .in_1(main_1_ir_out[10:8]), .in_2(main_1_ir_out[7:5]), .R_W(main_8_reg_dest), .in_4(multiplexer_2_out),
    .in_5(main_8_selpc_out), .clock(in_1), .out_7(out_5), .out_8(out_6));
  assign bit_extender_2_out = {{8{1'b0}}, main_1_ir_out[7:0]};  // Bit_Extender bit_extender_2
  assign bit_extender_3_out = {{5{1'b0}}, main_1_ir_out[10:0]};  // Bit_Extender bit_extender_3
  Multiplexer #(.width(16)) multiplexer_2 (.in0(out_8), .in1(in_3), .out(multiplexer_2_out), .sel(in_4));  // open: en
  Memory_register_main main_4 (
    .PC_in(main_1_pc_out), .PC_4_in(main_1_pc_4_out), .IR_in(main_1_ir_out), .regDst(main_2_regdst),
    .RegWr(main_2_regwr), .Extop(main_2_extop), .AluSrc(main_2_alusrc), .MemRd(main_2_memrd),
    .MemWrite_in(main_2_memwr), .Wbdata(main_2_wbdata), .jump(main_2_j_instruction),
    .Op_code(main_1_ir_out[15:11]), .function_bit(main_1_ir_out[1:0]), .IMM_in(bit_extender_1_out),
    .shamt_in(multiplexer_1_out), .v0_in(bit_extender_2_out), .a0_in(bit_extender_3_out), .RF_R1_in(out_5),
    .RF_R2_in(out_6), .clk(in_1), .PC_out(main_4_pc_out), .PC_4_out(main_4_pc_4_out), .IR_out(main_4_ir_out),
    .RegWr_2(main_4_regwr_2), .AluSrc_2(main_4_alusrc_2), .MemRd_2(main_4_memrd_2),
    .MemWrite_out(main_4_memwrite_out), .Wbdata_2(main_4_wbdata_2), .jump_2(Jump),
    .Op_code_2(main_4_op_code_2), .function_bit_2(main_4_function_bit_2), .IMM_out(main_4_imm_out),
    .shamt_out(main_4_shamt_out), .v0_out(main_4_v0_out), .a0_out(main_4_a0_out),
    .RF_R1_out(main_4_rf_r1_out), .RF_R2_out(main_4_rf_r2_out));  // open: Addr_in, clear, regDst_2, Extop_2, Addr_out
  Multiplexer #(.width(16)) multiplexer_3 (
    .in0(main_4_rf_r2_out), .in1(main_4_imm_out), .out(multiplexer_3_out), .sel(main_4_alusrc_2));  // open: en
  not not_2 (not_2_out, Branch);
  ALU1_main main_5 (
    .Bus_A(main_4_rf_r1_out), .Bus_B(multiplexer_3_out), .Function_bit(main_6_function_bit_2),
    .Alu_Selection(main_6_alu_selection), .Branch_Selection(main_6_branch_output), .Branch(Branch),
    .Bus_w(out_7));
  ALu_controller_main main_6 (
    .Op_code(main_4_op_code_2), .Function_bit(main_4_function_bit_2), .Branch_output(main_6_branch_output),
    .Function_bit_2(main_6_function_bit_2), .Alu_Selection(main_6_alu_selection));
  Multiplexer #(.width(16)) multiplexer_4 (
    .in0(main_4_v0_out), .in1(main_4_a0_out), .out(data), .sel(or_2_out));  // open: en
  or or_2 (or_2_out, not_2_out, Jump);
  ALu_register_main main_7 (
    .PC_in(main_4_pc_out), .PC_4_in(main_4_pc_4_out), .IR_in(main_4_ir_out), .selPC_in(main_4_regwr_2),
    .RF_Din_in(main_4_wbdata_2), .MemWrite_in(main_4_memrd_2), .RegWrite_in(main_4_memwrite_out),
    .halt_in(main_4_shamt_out), .RF_R1_in(out_7), .RF_R2_in(main_4_rf_r2_out), .clk(in_1),
    .PC_out(main_7_pc_out), .PC_4_out(main_7_pc_4_out), .IR_out(main_7_ir_out), .selPC_out(main_7_selpc_out),
    .RF_Din_out(main_7_rf_din_out), .MemWrite_out(main_7_memwrite_out), .RegWrite_out(main_7_regwrite_out),
    .halt_out(main_7_halt_out), .RF_R1_out(main_7_rf_r1_out), .RF_R2_out(main_7_rf_r2_out));  // open: RW__in, Lo_in, Hi_in, Branch_in, equal_in, S_EXT_in, ALU_out_in, Addr_in, clear, RW__out, Lo_out, Hi_out, Branch_out, equal_out, S_EXT_out, ALU_out_out, Addr_out
  or or_3 (or_3_out, main_7_regwrite_out, main_7_memwrite_out);
  RAM #(.addrWidth(16), .dataWidth(16), .bus("separate")) ram_1 (
    .addr(main_7_rf_r1_out), .din(main_7_rf_r2_out), .data(ram_1_data), .str(main_7_regwrite_out),
    .sel(or_3_out), .clk(in_1), .ld(main_7_memwrite_out));  // open: clr
  Multiplexer #(.width(16)) multiplexer_5 (
    .in0(main_7_rf_r1_out), .in1(ram_1_data), .out(multiplexer_5_out), .sel(main_7_rf_din_out));  // open: en
  Regwrite_Register_main main_8 (
    .PC_in(main_7_pc_out), .PC_4_in(main_7_pc_4_out), .IR_in(main_7_ir_out), .selPC_in(main_7_selpc_out),
    .Lo_in(multiplexer_5_out), .regdet(main_7_halt_out), .clk(in_1), .selPC_out(main_8_selpc_out),
    .Lo_out(out_8), .reg_dest(main_8_reg_dest));  // open: RW__in, RF_Din_in, DM_out_in, RegWrite_in, Hi_in, Branch_in, equal_in, halt_in, ALU_out_in, Addr_in, RF_R1_in, clear, PC_out, PC_4_out, IR_out, RW__out, RF_Din_out, DM_out_out, RegWrite_out, Hi_out, Branch_out, equal_out, halt_out, ALU_out_out, Addr_out, RF_R1_out

  // Other names for the same wires on the sheet: Alu_result[15:0] = out_7; Clock = in_1; Ra[15:0] = out_5;
  //   Rb[15:0] = out_6; regwrite[15:0] = out_8; set_manually_Rw[15:0] = in_3

  // Notes on the sheet:
  //   contents of rom_1 (hex, n*v repeats v):
  //   0 14c 14d 14e 94c 94d 94e 94f 14f 94c 94d 94e 94f
endmodule
