// Logisim project B-type.circ as structural Verilog
module I_type_Detectot (
  input  A4,
  input  A3,
  input  A2,
  input  A1,
  input  A0,
  output I
);

  wire and_1_out, and_2_out, and_3_out, not_1_out, not_2_out, not_3_out, not_4_out, not_5_out, not_6_out;

  not not_1 (not_1_out, A4);
  not not_2 (not_2_out, A3);
  not not_3 (not_3_out, A4);
  not not_4 (not_4_out, A2);
  not not_5 (not_5_out, A4);
  not not_6 (not_6_out, A1);
  and and_1 (and_1_out, not_1_out, not_2_out, A2);
  and and_2 (and_2_out, not_3_out, A3, not_4_out);
  and and_3 (and_3_out, not_5_out, A3, not_6_out);
  or or_1 (I, and_1_out, and_2_out, and_3_out);
endmodule

module B_type_Dectector (
  input  A4,
  input  A3,
  input  A2,
  input  A1,
  input  A0,
  output B
);

  wire and_1_out, and_2_out, not_1_out, not_2_out;

  not not_1 (not_1_out, A3);
  not not_2 (not_2_out, A2);
  and and_1 (and_1_out, A4, not_1_out, A2);
  and and_2 (and_2_out, A4, A3, not_2_out);
  or or_1 (B, and_1_out, and_2_out);
endmodule
