// Logisim project Branch comparator.circ as structural Verilog: 1 circuit, main circuit main
module main (
  input  [15:0] bus_A,
  input  [2:0] Selelction,
  output Branch,
  output [15:0] Output
);

  wire comparator_1_eq, comparator_1_gt, comparator_1_lt, not_1_out, or_1_out, or_2_out;
  wire [15:0] bit_extender_1_out;

  assign bit_extender_1_out = {{15{1'b0}}, 1'b0};  // Bit_Extender bit_extender_1
  Comparator #(.width(16)) comparator_1 (
    .a(bus_A), .b(bit_extender_1_out), .gt(comparator_1_gt), .eq(comparator_1_eq), .lt(comparator_1_lt));
  or or_1 (or_1_out, comparator_1_gt, comparator_1_eq);
  not not_1 (not_1_out, comparator_1_eq);
  or or_2 (or_2_out, comparator_1_lt, comparator_1_eq);
  Multiplexer #(.select(3)) multiplexer_1 (
    .in0(comparator_1_eq), .in1(not_1_out), .in2(comparator_1_lt), .in3(or_1_out), .in4(comparator_1_gt),
    .in5(or_2_out), .out(Branch), .sel(Selelction));  // open: in6, in7, en
  assign Output = {{15{1'b0}}, Branch};  // Bit_Extender bit_extender_2
endmodule
