// Logisim project Datapath Memoer.circ as structural Verilog: 1 circuit, main circuit main
module main (
  input  [2:0] RB,
  input  [2:0] RB_2,
  input  [2:0] RW,
  input  [15:0] in_4,
  input  REG_WRITE,
  input  CLOCK,
  output [15:0] out_7,
  output [15:0] out_8
);

  memory_element_main main_1 (
    .in_1(RB), .in_2(RB_2), .R_W(RW), .in_4(in_4), .in_5(REG_WRITE), .clock(CLOCK), .out_7(out_7),
    .out_8(out_8));

  // Notes on the sheet:
  //   16 bit Rw bus
  //   RA Bus
  //   RB Bus
endmodule
