// Logisim project I-type instruction.circ as structural Verilog: 1 circuit, main circuit main
module main (
  input  in_1,
  input  in_2,
  input  in_3,
  input  in_4,
  input  in_5,
  input  in_6,
  input  [15:0] in_7,
  output [15:0] out_8,
  output [15:0] out_9,
  output [15:0] out_10
);

  wire [1:0] ram_1_data_3;
  wire [2:0] multiplexer_1_out;
  wire [4:0] ram_1_data_2;
  wire [10:2] ram_1_data;
  wire [15:0] bit_extender_1_out, counter_1_q, multiplexer_2_out;

  Counter #(.width(16), .max('hffff)) counter_1 (
    .Q(counter_1_q), .clk(in_3), .clr(in_4));  // open: load, D, count, carry
  RAM #(.addrWidth(16), .dataWidth(16)) ram_1 (
    .addr(counter_1_q), .data({ram_1_data_2, ram_1_data, ram_1_data_3}), .clk(in_3));  // open: sel, ld, clr
  assign bit_extender_1_out = {{11{1'b0}}, {ram_1_data[4:2], ram_1_data_3}};  // Bit_Extender bit_extender_1
  Multiplexer #(.width(3)) multiplexer_1 (
    .in0(ram_1_data[7:5]), .in1(ram_1_data[4:2]), .out(multiplexer_1_out), .sel(in_2));  // open: en
  memory_element_main main_1 (
    .in_1(ram_1_data[10:8]), .in_2(ram_1_data[7:5]), .R_W(multiplexer_1_out), .in_4(in_7), .in_5(in_3),
    .clock(in_6), .out_7(out_9), .out_8(out_10));
  Multiplexer #(.width(16)) multiplexer_2 (
    .in0(bit_extender_1_out), .in1(out_10), .out(multiplexer_2_out), .sel(in_1));  // open: en
  // ALU_main main_2: pin names not known; wires that end beside it: ram_1_data_2, out_9, multiplexer_2_out, in_5, ram_1_data_3, out_8, in_5
endmodule
