// Logisim project I-type without shifter.circ as structural Verilog: 2 circuits, main circuit main
module main (
  input  [4:0] in_1,
  input  [1:0] in_2,
  output [1:0] Function_bit
);

  wire b_type_dectector_1_b, J_type_out, lw_out, R_type_out, sw_out, undriven;

  assign Function_bit = R_type_out ? in_2 : 2'bz;  // Controlled_Buffer controlled_buffer_1
  and R_type (R_type_out, ~in_1[4], ~in_1[3], ~in_1[2], ~in_1[1]);  // AND_Gate
  and lw (lw_out, in_1[4], ~in_1[3], ~in_1[2], ~in_1[1], ~in_1[0]);  // AND_Gate
  assign Function_bit = undriven ? in_1[1:0] : 2'bz;  // Controlled_Buffer controlled_buffer_2
  and sw (sw_out, in_1[4], ~in_1[3], ~in_1[2], ~in_1[1], in_1[0]);  // AND_Gate
  and J_type (J_type_out, in_1[4], in_1[3], in_1[2], in_1[1]);
  B_type_Dectector b_type_dectector_1 (
    .A4(in_1[4]), .A3(in_1[3]), .A2(in_1[2]), .A1(in_1[1]), .A0(in_1[0]), .B(b_type_dectector_1_b));
endmodule

module I_type_without_shifter (
  input  A4,
  input  A3,
  input  A2,
  input  A1,
  input  A0,
  output I
);

  wire and_1_out, and_2_out, not_1_out, not_2_out, not_3_out, not_4_out;

  not not_1 (not_1_out, A4);
  not not_2 (not_2_out, A3);
  not not_3 (not_3_out, A4);
  not not_4 (not_4_out, A2);
  and and_1 (and_1_out, not_1_out, not_2_out, A2);
  and and_2 (and_2_out, not_3_out, A3, not_4_out);
  or or_1 (I, and_1_out, and_2_out);
endmodule
