// Logisim project Next Program counter.circ as structural Verilog: 1 circuit, main circuit main
module main (
  input  [15:0] in_1,
  input  [15:0] in_2,
  input  [10:0] in_3,
  input  in_4,
  output [15:0] out_5
);

  wire [15:0] adder_1_out;

  Adder #(.width(16)) adder_1 (.a(in_1), .b(in_2), .out(adder_1_out));  // open: cin, cout
  Multiplexer #(.width(16)) multiplexer_1 (
    .in0(adder_1_out), .in1({in_1[15:11], in_3}), .out(out_5), .sel(in_4));  // open: en
endmodule
