// Logisim project single cycle processor_R.circ as structural Verilog: 1 circuit, main circuit main
module main (
  input  Pc_reset_pin,
  input  [15:0] in_2,
  input  Set_manually,
  output [15:0] out_4,
  output [15:0] out_5,
  output [15:0] out_6,
  output [15:0] out_7,
  output [15:0] out_8
);

  wire clock_2_out, j_or_branch_out, main_1_alusrc, main_1_j_instruction, main_1_memrd, main_1_memwr,
       main_1_regdst, main_1_regwr, main_1_wbdata, main_2_branch, not_1_out, not_2_out, or_1_out, or_2_out;
  wire [1:0] Alu_controller_alu_selection, Alu_controller_function_bit_2, ram_1_data_2;
  wire [2:0] Alu_controller_branch_output, multiplexer_1_out;
  wire [15:0] bit_extender_1_out, bit_extender_2_out, bit_extender_3_out, counter_1_q, multiplexer_2_out,
       ram_2_data, Register_memory_out_8;
  wire [15:2] ram_1_data;

  or j_or_branch (j_or_branch_out, main_2_branch, main_1_j_instruction);
  Clock clock_1 ();  // open: out
  not not_1 (not_1_out, j_or_branch_out);
  Clock clock_2 (.out(clock_2_out));
  Counter #(.width(16), .max('hffff)) counter_1 (
    .load(j_or_branch_out), .D(bit_extender_2_out), .count(not_1_out), .Q(counter_1_q), .clk(clock_2_out),
    .clr(Pc_reset_pin));  // open: carry
  RAM #(.addrWidth(16), .dataWidth(16)) ram_1 (
    .addr(counter_1_q), .data({ram_1_data, ram_1_data_2}), .clk(clock_2_out));  // open: sel, ld, clr
  assign bit_extender_1_out = {{11{1'b0}}, {ram_1_data[4:2], ram_1_data_2}};  // Bit_Extender bit_extender_1
  Multiplexer #(.width(3)) multiplexer_1 (
    .in0(ram_1_data[7:5]), .in1(ram_1_data[4:2]), .out(multiplexer_1_out), .sel(main_1_regdst));  // open: en
  Control_unit_main main_1 (
    .in_1(ram_1_data[15:11]), .J_Instruction(main_1_j_instruction), .regDst(main_1_regdst),
    .RegWr(main_1_regwr), .AluSrc(main_1_alusrc), .MemRd(main_1_memrd), .MemWr(main_1_memwr),
    .WBdata(main_1_wbdata));  // open: Extop
  memory_element_main Register_memory (
    .in_1(ram_1_data[10:8]), .in_2(ram_1_data[7:5]), .R_W(multiplexer_1_out), .in_4(multiplexer_2_out),
    .in_5(main_1_regwr), .clock(clock_2_out), .out_7(out_6), .out_8(Register_memory_out_8));
  Multiplexer #(.width(16)) multiplexer_2 (
    .in0(out_8), .in1(in_2), .out(multiplexer_2_out), .sel(Set_manually));  // open: en
  assign bit_extender_2_out = {{8{1'b0}}, {ram_1_data[7:2], ram_1_data_2}};  // Bit_Extender bit_extender_2
  Multiplexer #(.width(16)) multiplexer_3 (
    .in0(Register_memory_out_8), .in1(bit_extender_1_out), .out(out_5), .sel(main_1_alusrc));  // open: en
  assign bit_extender_3_out = {{5{1'b0}}, {ram_1_data[10:2], ram_1_data_2}};  // Bit_Extender bit_extender_3
  ALU1_main main_2 (
    .Bus_A(out_6), .Bus_B(out_5), .Function_bit(Alu_controller_function_bit_2),
    .Alu_Selection(Alu_controller_alu_selection), .Branch_Selection(Alu_controller_branch_output),
    .Branch(main_2_branch), .Bus_w(out_7));
  ALu_controller_main Alu_controller (
    .Op_code(ram_1_data[15:11]), .Function_bit(ram_1_data_2), .Branch_output(Alu_controller_branch_output),
    .Function_bit_2(Alu_controller_function_bit_2), .Alu_Selection(Alu_controller_alu_selection));
  not not_2 (not_2_out, main_2_branch);
  or or_1 (or_1_out, not_2_out, main_1_j_instruction);
  Multiplexer #(.width(16)) multiplexer_4 (
    .in0(bit_extender_2_out), .in1(bit_extender_3_out), .out(out_4), .sel(or_1_out));  // open: en
  RAM #(.addrWidth(16), .dataWidth(16), .bus("separate")) ram_2 (
    .addr(out_7), .din(Register_memory_out_8), .data(ram_2_data), .str(main_1_memwr), .sel(or_2_out),
    .clk(clock_2_out), .ld(main_1_memrd));  // open: clr
  Multiplexer #(.width(16)) multiplexer_5 (
    .in0(out_7), .in1(ram_2_data), .out(out_8), .sel(main_1_wbdata));  // open: en
  or or_2 (or_2_out, main_1_memrd, main_1_memwr);

  // Notes on the sheet:
  //   Clock
  //   RW bus(set manually)
  //   Reg write
  //   Register Destination
  //   OP code 5 bits
  //   RB Bus
  //   ALu Source
  //   RA Bus
  //   Alu Result
endmodule
